# Fritzing sketch Laser guidance (saved by Fritzing 0.9.3b)
breadboards: 1

parts:
  Part2 = Bluetooth HC-05 Macho
  Part1 = Arduino Uno (Rev3)
  J1 = Basic Servo
  J2 = Basic Servo
  R1 = Resistor [tolerance=±5% resistance=220 package="0402 [SMD]"]
  LASER = LED - 5mm [color="Red (633nm)" package="5 mm [THT]"]

nets:
  N1: Part2.State, Part1.D12/MISO
  N2: Part2.TXD, Part1.D2
  N3: Part2.RXD, Part1.D3_PWM
  VCC: Part2.VCC, Part1.5V, J1.vcc, J2.vcc
  GND: Part2.GND, Part1.GND, J1.gnd, J2.gnd, LASER.cathode
  N4: Part1.D8, R1.Pin_0
  N5: Part1.D9_PWM, J2.pulse
  N6: Part1.D10_PWM/SS, J1.pulse
  N7: R1.Pin_1, LASER.anode

notes:
  LASER
  Horizontal and Vertical moving servo

// code stored in the sketch: Laser guidance 1.ino
#include<SoftwareSerial.h>
#include <Servo.h>
Servo m1;
Servo m2;//create Servo object m1 and m2
SoftwareSerial BTserial(2,3); //RX and TX;
int p1=0,p2=0,z=0;  //position of servo 1 and 2

void setup() 
{
  boolean Status=false;                     // status of bluetooth
   pinMode(8,OUTPUT);                       // for Laser
   pinMode(12,INPUT);                       // for detecting status of bluetooth
   pinMode(13,OUTPUT);                      //display status of bluetooth
  BTserial.begin(9600);                     //Initialise Serial communication via bluetooth
  m1.attach(9);                             // attaches the servo on pin 9 to the servo object
  m2.attach(10);                            // attaches the servo on pin 10 to the servo object
  while(!Status)
  {
    if(digitalRead(12)==HIGH)
      Status=true;
}
digitalWrite(13,HIGH);             // indicates that bluetooth is connected
}
void loop()
{ 
  if(BTserial.available()>0)
   z=BTserial.read();
{ 
                                    //For seervo m1
  while(z=='1')
  {
    m1.write(p1);
    p1=p1+5;                   // increment the angle by 5 degree when button is pressed
    if (p1>180)                //the max anlgle of servo is 180 degrees
    p1=180;
    delay(20);                //for stability
    break;
  }
   while(z=='2')
   {
    m1.write(p1);
    p1=p1-5;                        // decrement the angle by 5 degrees when the button is pressed
    if(p1<0)
    p1=0;                   // the minimum angle of servo is 0 degrees
    delay(20);             // for stability
    break;
   }
                            //Simialrly for servo m2
  while(z=='3')
  {
    m2.write(p2);
    p2=p2+5;                // increment the angle by 5 degree when button is pressed
    if (p2>180)
    p2=180;                 //the max anlgle of servo is 180 degrees
    delay(20);               //for stability
    break;
  }
   while(z=='4')
   {
    m2.write(p2);
    p2=p2-5;                // decrement the angle by 5 degrees when the button is pressed
    if(p2<0)
    p2=0;                  // the minimum angle of servo is 0 degrees
    delay(20);             //for stability
    break;
   }
   if (z=='0')// make servo object m1 to return to its initial position
   {
    m1.write(90);
    delay(20);
   }
   if (z=='9')  // make servo object m2 return to its initial position
   {
    m2.write(90);
    delay(20);
   }
   if (z=='a')           // To turn laser on
    digitalWrite(8,HIGH); 
   if (z=='b')          // To turn laser off
  digitalWrite(8,LOW); 
  }
}
